// Logisim project PipelinedProcessor.circ as structural Verilog: 6 circuits, main circuit Register File
module Register_File (
  input  [4:0] RW,
  input  [4:0] RA,
  input  [31:0] BusW,
  input  Register_Write,
  input  [4:0] RB,
  output [31:0] BusA,
  output [31:0] BusB
);

  wire and_1_out, and_2_out, and_3_out, and_4_out, and_5_out, and_6_out, and_7_out, and_8_out, and_9_out,
       and_10_out, and_11_out, and_12_out, and_13_out, and_14_out, and_15_out, and_16_out, and_17_out,
       and_18_out, and_19_out, and_20_out, and_21_out, and_22_out, and_23_out, and_24_out, and_25_out,
       and_26_out, and_27_out, and_28_out, and_29_out, and_30_out, and_31_out, CLK, L1, L2, L3, L4, L5, L6,
       L7, L8, L9, L10, L11, L12, L13, L14, L15, L16, L17, L18, L19, L20, L21, L22, L23, L24, L25, L26, L27,
       L28, L29, L30, L31;
  wire [31:0] O1, O2, O3, O4, O5, O6, O7, O8, O9, O10, O11, O12, O13, O14, O15, O16, O17, O18, O19, O20, O21,
       O22, O23, O24, O25, O26, O27, O28, O29, O30, O31;

  Clock clock_1 (.out(CLK));
  Decoder #(.select(5)) decoder_1 (
    .out1(L1), .out2(L2), .out3(L3), .out4(L4), .out5(L5), .out6(L6), .out7(L7), .out8(L8), .out9(L9),
    .out10(L10), .out11(L11), .out12(L12), .out13(L13), .out14(L14), .out15(L15), .out16(L16), .out17(L17),
    .out18(L18), .out19(L19), .out20(L20), .out21(L21), .out22(L22), .out23(L23), .out24(L24), .out25(L25),
    .out26(L26), .out27(L27), .out28(L28), .out29(L29), .out30(L30), .out31(L31), .sel(RW));  // open: out0, en
  and and_1 (and_1_out, L1, Register_Write);
  and and_2 (and_2_out, L2, Register_Write);
  and and_3 (and_3_out, L3, Register_Write);
  and and_4 (and_4_out, L4, Register_Write);
  and and_5 (and_5_out, L5, Register_Write);
  and and_6 (and_6_out, L6, Register_Write);
  and and_7 (and_7_out, L7, Register_Write);
  and and_8 (and_8_out, L8, Register_Write);
  and and_9 (and_9_out, L9, Register_Write);
  and and_10 (and_10_out, L10, Register_Write);
  and and_11 (and_11_out, L11, Register_Write);
  and and_12 (and_12_out, L12, Register_Write);
  and and_13 (and_13_out, L13, Register_Write);
  and and_14 (and_14_out, L14, Register_Write);
  and and_15 (and_15_out, L15, Register_Write);
  and and_16 (and_16_out, L16, Register_Write);
  and and_17 (and_17_out, L17, Register_Write);
  and and_18 (and_18_out, L18, Register_Write);
  and and_19 (and_19_out, L19, Register_Write);
  and and_20 (and_20_out, L20, Register_Write);
  and and_21 (and_21_out, L21, Register_Write);
  and and_22 (and_22_out, L22, Register_Write);
  and and_23 (and_23_out, L23, Register_Write);
  and and_24 (and_24_out, L24, Register_Write);
  and and_25 (and_25_out, L25, Register_Write);
  and and_26 (and_26_out, L26, Register_Write);
  and and_27 (and_27_out, L27, Register_Write);
  and and_28 (and_28_out, L28, Register_Write);
  and and_29 (and_29_out, L29, Register_Write);
  and and_30 (and_30_out, L30, Register_Write);
  and and_31 (and_31_out, L31, Register_Write);
  Register #(.width(32)) R1 (.D(BusW), .en(and_1_out), .Q(O1), .clk(CLK));  // open: clr
  Register #(.width(32)) R2 (.D(BusW), .en(and_2_out), .Q(O2), .clk(CLK));  // open: clr
  Register #(.width(32)) R3 (.D(BusW), .en(and_3_out), .Q(O3), .clk(CLK));  // open: clr
  Register #(.width(32)) R4 (.D(BusW), .en(and_4_out), .Q(O4), .clk(CLK));  // open: clr
  Register #(.width(32)) R5 (.D(BusW), .en(and_5_out), .Q(O5), .clk(CLK));  // open: clr
  Register #(.width(32)) R6 (.D(BusW), .en(and_6_out), .Q(O6), .clk(CLK));  // open: clr
  Register #(.width(32)) R7 (.D(BusW), .en(and_7_out), .Q(O7), .clk(CLK));  // open: clr
  Register #(.width(32)) R8 (.D(BusW), .en(and_8_out), .Q(O8), .clk(CLK));  // open: clr
  Register #(.width(32)) R9 (.D(BusW), .en(and_9_out), .Q(O9), .clk(CLK));  // open: clr
  Register #(.width(32)) R10 (.D(BusW), .en(and_10_out), .Q(O10), .clk(CLK));  // open: clr
  Register #(.width(32)) R11 (.D(BusW), .en(and_11_out), .Q(O11), .clk(CLK));  // open: clr
  Register #(.width(32)) R12 (.D(BusW), .en(and_12_out), .Q(O12), .clk(CLK));  // open: clr
  Register #(.width(32)) R13 (.D(BusW), .en(and_13_out), .Q(O13), .clk(CLK));  // open: clr
  Register #(.width(32)) R14 (.D(BusW), .en(and_14_out), .Q(O14), .clk(CLK));  // open: clr
  Register #(.width(32)) R15 (.D(BusW), .en(and_15_out), .Q(O15), .clk(CLK));  // open: clr
  Register #(.width(32)) R16 (.D(BusW), .en(and_16_out), .Q(O16), .clk(CLK));  // open: clr
  Register #(.width(32)) R17 (.D(BusW), .en(and_17_out), .Q(O17), .clk(CLK));  // open: clr
  Register #(.width(32)) R18 (.D(BusW), .en(and_18_out), .Q(O18), .clk(CLK));  // open: clr
  Register #(.width(32)) R19 (.D(BusW), .en(and_19_out), .Q(O19), .clk(CLK));  // open: clr
  Register #(.width(32)) R20 (.D(BusW), .en(and_20_out), .Q(O20), .clk(CLK));  // open: clr
  Register #(.width(32)) R21 (.D(BusW), .en(and_21_out), .Q(O21), .clk(CLK));  // open: clr
  Register #(.width(32)) R22 (.D(BusW), .en(and_22_out), .Q(O22), .clk(CLK));  // open: clr
  Register #(.width(32)) R23 (.D(BusW), .en(and_23_out), .Q(O23), .clk(CLK));  // open: clr
  Register #(.width(32)) R24 (.D(BusW), .en(and_24_out), .Q(O24), .clk(CLK));  // open: clr
  Register #(.width(32)) R25 (.D(BusW), .en(and_25_out), .Q(O25), .clk(CLK));  // open: clr
  Register #(.width(32)) R26 (.D(BusW), .en(and_26_out), .Q(O26), .clk(CLK));  // open: clr
  Register #(.width(32)) R27 (.D(BusW), .en(and_27_out), .Q(O27), .clk(CLK));  // open: clr
  Register #(.width(32)) R28 (.D(BusW), .en(and_28_out), .Q(O28), .clk(CLK));  // open: clr
  Register #(.width(32)) R29 (.D(BusW), .en(and_29_out), .Q(O29), .clk(CLK));  // open: clr
  Register #(.width(32)) R30 (.D(BusW), .en(and_30_out), .Q(O30), .clk(CLK));  // open: clr
  Register #(.width(32)) R31 (.D(BusW), .en(and_31_out), .Q(O31), .clk(CLK));  // open: clr
  Multiplexer #(.select(5), .width(32)) multiplexer_1 (
    .in0({32{1'b0}}), .in1(O1), .in2(O2), .in3(O3), .in4(O4), .in5(O5), .in6(O6), .in7(O7), .in8(O8),
    .in9(O9), .in10(O10), .in11(O11), .in12(O12), .in13(O13), .in14(O14), .in15(O15), .in16(O16), .in17(O17),
    .in18(O18), .in19(O19), .in20(O20), .in21(O21), .in22(O22), .in23(O23), .in24(O24), .in25(O25),
    .in26(O26), .in27(O27), .in28(O28), .in29(O29), .in30(O30), .in31(O31), .out(BusA), .sel(RA));  // open: en
  Multiplexer #(.select(5), .width(32)) multiplexer_2 (
    .in0({32{1'b0}}), .in1(O1), .in2(O2), .in3(O3), .in4(O4), .in5(O5), .in6(O6), .in7(O7), .in8(O8),
    .in9(O9), .in10(O10), .in11(O11), .in12(O12), .in13(O13), .in14(O14), .in15(O15), .in16(O16), .in17(O17),
    .in18(O18), .in19(O19), .in20(O20), .in21(O21), .in22(O22), .in23(O23), .in24(O24), .in25(O25),
    .in26(O26), .in27(O27), .in28(O28), .in29(O29), .in30(O30), .in31(O31), .out(BusB), .sel(RB));  // open: en

  // Other names for the same wires on the sheet: WB = Register_Write
endmodule

module ALU (
  input  [31:0] A,
  input  [31:0] B,
  input  [3:0] ALU_Selcetion,
  output [31:0] ALU_Result,
  output Zero
);

  wire SGT, SLT;
  wire [31:0] adder_1_out, and_1_out, bit_extender_1_out, bit_extender_2_out, bit_extender_3_out,
       bit_extender_4_out, multiplier_1_out, not_1_out, or_1_out, shifter_1_out, shifter_2_out,
       shifter_3_out, shifter_4_out, shifter_5_out, subtractor_1_out, xor_1_out;

  Comparator #(.width(32)) comparator_1 (.a(A), .b(B), .gt(SGT), .lt(SLT));  // open: eq
  Shifter #(.width(32)) shifter_1 (.in(A), .\dist (B[4:0]), .out(shifter_1_out));
  Shifter #(.width(32), .shift("lr")) shifter_2 (.in(A), .\dist (B[4:0]), .out(shifter_2_out));
  Shifter #(.width(32), .shift("ar")) shifter_3 (.in(A), .\dist (B[4:0]), .out(shifter_3_out));
  Shifter #(.width(32), .shift("rr")) shifter_4 (.in(A), .\dist (B[4:0]), .out(shifter_4_out));
  Adder #(.width(32)) adder_1 (.a(A), .b(B), .out(adder_1_out));  // open: cin, cout
  Subtractor #(.width(32)) subtractor_1 (.a(A), .b(B), .out(subtractor_1_out));  // open: bin, bout
  assign bit_extender_1_out = {{31{SLT}}, SLT};  // Bit_Extender bit_extender_1
  assign bit_extender_2_out = {{31{1'b0}}, SLT};  // Bit_Extender bit_extender_2
  assign xor_1_out = A ^ B;  // XOR_Gate xor_1, 32 bits wide
  assign or_1_out = A | B;  // OR_Gate or_1, 32 bits wide
  assign and_1_out = A & B;  // AND_Gate and_1, 32 bits wide
  Multiplier #(.width(32)) multiplier_1 (.a(A), .b(B), .out(multiplier_1_out));  // open: cin, cout
  Shifter #(.width(32)) shifter_5 (.in(B), .\dist (5'b10000), .out(shifter_5_out));
  assign bit_extender_3_out = {{31{SGT}}, SGT};  // Bit_Extender bit_extender_3
  assign bit_extender_4_out = {{31{1'b0}}, SGT};  // Bit_Extender bit_extender_4
  assign not_1_out = ~or_1_out;  // NOT_Gate not_1, 32 bits wide
  Multiplexer #(.select(4), .width(32)) multiplexer_1 (
    .in0(shifter_1_out), .in1(shifter_2_out), .in2(shifter_3_out), .in3(shifter_4_out), .in4(adder_1_out),
    .in5(subtractor_1_out), .in6(bit_extender_1_out), .in7(bit_extender_2_out), .in8(xor_1_out),
    .in9(or_1_out), .in10(and_1_out), .in11(not_1_out), .in12(multiplier_1_out), .in13(shifter_5_out),
    .in14(bit_extender_3_out), .in15(bit_extender_4_out), .out(ALU_Result), .sel(ALU_Selcetion));  // open: en
  nor nor_1 (Zero, ALU_Result[0], ALU_Result[1], ALU_Result[2], ALU_Result[3], ALU_Result[4], ALU_Result[5], ALU_Result[6], ALU_Result[7], ALU_Result[8], ALU_Result[9], ALU_Result[10], ALU_Result[11], ALU_Result[12], ALU_Result[13], ALU_Result[14], ALU_Result[15], ALU_Result[16], ALU_Result[17], ALU_Result[18], ALU_Result[19], ALU_Result[20], ALU_Result[21], ALU_Result[22], ALU_Result[23], ALU_Result[24], ALU_Result[25], ALU_Result[26], ALU_Result[27], ALU_Result[28], ALU_Result[29], ALU_Result[30], ALU_Result[31]);

  // Other names for the same wires on the sheet: SGTU = SGT; SLTU = SLT

  // Notes on the sheet:
  //   Shift by 16
endmodule

module Control_Unit (
  input  [5:0] OpCode,
  input  [10:0] Function,
  output [6:0] Controller,
  output [6:0] ALU_Op,
  output JALR,
  output BEQ,
  output BNE,
  output BLT,
  output BGE,
  output BLTU,
  output BGEU
);

  wire comparator_1_eq;
  wire [6:0] rom_2_data;

  Comparator #(.width(6), .mode("unsigned")) comparator_1 (
    .a(OpCode), .b({6{1'b0}}), .eq(comparator_1_eq));  // open: gt, lt
  ROM #(.addrWidth(6), .dataWidth(7)) rom_1 (.addr(OpCode), .data(Controller));  // open: sel
  ROM #(.addrWidth(6), .dataWidth(7)) rom_2 (.addr(OpCode), .data(rom_2_data));  // open: sel
  and u_JALR (JALR, ~OpCode[5], ~OpCode[4], OpCode[3], OpCode[2], ~OpCode[1], OpCode[0]);  // AND_Gate
  and BQE (BEQ, ~OpCode[5], OpCode[4], ~OpCode[3], ~OpCode[2], ~OpCode[1], ~OpCode[0]);  // AND_Gate
  Multiplexer #(.width(7)) multiplexer_1 (
    .in0(rom_2_data), .in1(Function[6:0]), .out(ALU_Op), .sel(comparator_1_eq));  // open: en
  and u_BNE (BNE, ~OpCode[5], OpCode[4], ~OpCode[3], ~OpCode[2], ~OpCode[1], OpCode[0]);  // AND_Gate
  and u_BLT (BLT, ~OpCode[5], OpCode[4], ~OpCode[3], ~OpCode[2], OpCode[1], ~OpCode[0]);  // AND_Gate
  and u_BGE (BGE, ~OpCode[5], OpCode[4], ~OpCode[3], ~OpCode[2], OpCode[1], OpCode[0]);  // AND_Gate
  and u_BLTU (BLTU, ~OpCode[5], OpCode[4], ~OpCode[3], OpCode[2], ~OpCode[1], ~OpCode[0]);  // AND_Gate
  and u_BGEU (BGEU, ~OpCode[5], OpCode[4], ~OpCode[3], OpCode[2], ~OpCode[1], OpCode[0]);  // AND_Gate

  // Notes on the sheet:
  //   R-Type
  //   contents of rom_1 (hex, n*v repeats v):
  //   40 4*70 50 50 50 4*60 50 52 55 38
  //   contents of rom_2 (hex, n*v repeats v):
  //   0 0 1 2 3 4 6 7 8 9 a b d 0 4 4 5 5 6 e 7 f
  //   non-R-Type
  //   R-Type
endmodule

module NextPC (
  input  [19:0] Inc_PC,
  input  [31:0] Imm11_5S,
  input  [31:0] Ra,
  input  Zero,
  input  J,
  input  BQE,
  input  BNE,
  input  BLT,
  input  BGE,
  input  BLTU,
  input  BGEU,
  input  [15:0] imm16,
  output PCsrc_Kill1,
  output Kill2,
  output [19:0] Target_Addres
);

  wire and_1_out, and_2_out, and_3_out, and_4_out, and_5_out, and_6_out, clock_1_out, not_1_out, not_2_out,
       not_3_out, not_4_out, not_5_out;
  wire [19:0] adder_1_out, adder_2_out, adder_3_out, bit_extender_1_out, register_1_q;

  Adder #(.width(20)) adder_1 (.a(Inc_PC), .b(Imm11_5S[19:0]), .out(adder_1_out));  // open: cin, cout
  assign bit_extender_1_out = {{4{imm16[15]}}, imm16};  // Bit_Extender bit_extender_1
  Adder #(.width(20)) adder_2 (.a(adder_1_out), .b(20'h1), .out(adder_2_out));  // open: cin, cout
  Clock clock_1 (.out(clock_1_out));
  Adder #(.width(20)) adder_3 (.a(Ra[19:0]), .b(bit_extender_1_out), .out(adder_3_out));  // open: cin, cout
  // Probe on adder_3_out
  Register #(.width(20)) register_1 (.D(adder_2_out), .Q(register_1_q), .clk(clock_1_out));  // open: en, clr
  Multiplexer #(.width(20)) multiplexer_1 (
    .in0(register_1_q), .in1(adder_3_out), .out(Target_Addres), .sel(J));  // open: en
  or or_1 (PCsrc_Kill1, J, Kill2);
  and and_1 (and_1_out, BQE, Zero);
  and and_2 (and_2_out, BNE, not_1_out);
  not not_1 (not_1_out, Zero);
  or or_2 (Kill2, and_1_out, and_2_out, and_3_out, and_4_out, and_5_out, and_6_out);
  and and_3 (and_3_out, BLT, not_2_out);
  not not_2 (not_2_out, Zero);
  and and_4 (and_4_out, BGE, not_3_out);
  and and_5 (and_5_out, BLTU, not_4_out);
  not not_3 (not_3_out, Zero);
  and and_6 (and_6_out, BGEU, not_5_out);
  not not_4 (not_4_out, Zero);
  not not_5 (not_5_out, Zero);
endmodule

module Hazard_Detector (
  input  [4:0] rs1,
  input  [4:0] rs2,
  input  [4:0] Rd2,
  input  [4:0] Rd3,
  input  [4:0] Rd4,
  input  RegWr1,
  input  RegWr2,
  input  RegWr3,
  input  EX_MemRd,
  output [1:0] ForwardA,
  output [1:0] ForwardB,
  output Stall
);

  wire comparator_1_eq, comparator_2_eq, Input1A, Input1B, Input2A, Input2B, Input3A, Input3B, nor_1_out,
       nor_2_out, or_1_out, rs1_not_zero, rs1_Rd2, rs1_Rd3, rs1_Rd4, rs2_not_zero, rs2_Rd2, rs2_Rd3, rs2_Rd4;

  Comparator #(.width(5)) comparator_1 (.a(rs1), .b({5{1'b0}}), .eq(comparator_1_eq));  // open: gt, lt
  Comparator #(.width(5)) comparator_2 (.a(rs2), .b({5{1'b0}}), .eq(comparator_2_eq));  // open: gt, lt
  Comparator #(.width(5)) comparator_3 (.a(rs1), .b(Rd2), .eq(rs1_Rd2));  // open: gt, lt
  Comparator #(.width(5)) comparator_4 (.a(rs1), .b(Rd3), .eq(rs1_Rd3));  // open: gt, lt
  Comparator #(.width(5)) comparator_5 (.a(rs1), .b(Rd4), .eq(rs1_Rd4));  // open: gt, lt
  Comparator #(.width(5)) comparator_6 (.a(rs2), .b(Rd2), .eq(rs2_Rd2));  // open: gt, lt
  Comparator #(.width(5)) comparator_7 (.a(rs2), .b(Rd3), .eq(rs2_Rd3));  // open: gt, lt
  Comparator #(.width(5)) comparator_8 (.a(rs2), .b(Rd4), .eq(rs2_Rd4));  // open: gt, lt
  not not_1 (rs1_not_zero, comparator_1_eq);
  not not_2 (rs2_not_zero, comparator_2_eq);
  and and_1 (Input1A, rs1_not_zero, rs1_Rd2, RegWr1);
  and and_2 (Input2A, rs1_not_zero, rs1_Rd3, RegWr2, ~Input1A);  // AND_Gate
  and and_3 (Input3A, rs1_not_zero, rs1_Rd4, RegWr3, ~Input1A, ~Input2A);  // AND_Gate
  and and_4 (Input1B, rs2_not_zero, rs2_Rd2, RegWr1);
  and and_5 (Input2B, rs2_not_zero, rs2_Rd3, RegWr2, ~Input1B);  // AND_Gate
  and and_6 (Input3B, rs2_not_zero, rs2_Rd4, RegWr3, ~Input1B, ~Input2B);  // AND_Gate
  or or_1 (or_1_out, Input1A, Input1B);
  assign ForwardA = Input1A ? 2'b01 : 2'bz;  // Controlled_Buffer controlled_buffer_1
  assign ForwardA = Input2A ? 2'b10 : 2'bz;  // Controlled_Buffer controlled_buffer_2
  assign ForwardA = Input3A ? 2'b11 : 2'bz;  // Controlled_Buffer controlled_buffer_3
  nor nor_1 (nor_1_out, Input1A, Input2A, Input3A);
  assign ForwardA = nor_1_out ? 2'b00 : 2'bz;  // Controlled_Buffer controlled_buffer_4
  assign ForwardB = Input1B ? 2'b01 : 2'bz;  // Controlled_Buffer controlled_buffer_5
  assign ForwardB = Input2B ? 2'b10 : 2'bz;  // Controlled_Buffer controlled_buffer_6
  assign ForwardB = Input3B ? 2'b11 : 2'bz;  // Controlled_Buffer controlled_buffer_7
  nor nor_2 (nor_2_out, Input1B, Input2B, Input3B);
  assign ForwardB = nor_2_out ? 2'b00 : 2'bz;  // Controlled_Buffer controlled_buffer_8
  and and_7 (Stall, EX_MemRd, or_1_out);

  // Other names for the same wires on the sheet: Forward1A[1:0] = ForwardA; Forward2A[1:0] = ForwardA;
  //   Forward3A[1:0] = ForwardA; Forward1B[1:0] = ForwardB; Forward2B[1:0] = ForwardB; Forward3B[1:0] = ForwardB
endmodule

module Pipelined_Processor (
  input  in_1
);

  wire BEQ, BGE, BGEU, BLT, BLTU, BNE, CLK, control_unit_1_beq, control_unit_1_bge, control_unit_1_bgeu,
       control_unit_1_blt, control_unit_1_bltu, control_unit_1_bne, control_unit_1_jalr, Disable, EX_MemRd,
       J, Kill2, MemR, MemW, or_1_out, PCsrc, RegWrite1, RegWrite2, RegWrite3, Stall, Zero;
  wire [1:0] busBsrc, busWsrc, ForwardA, ForwardB;
  wire [3:0] aluOP, EX_q;
  wire [4:0] Rd2, Rd3, Rd4, rd_imm5L, rs1, rs2;
  wire [5:0] OpCode, WB_q;
  wire [5:4] MEM_q;
  wire [6:0] control_unit_1_alu_op, control_unit_1_controller, multiplexer_5_out, multiplexer_6_out;
  wire [6:4] EX_2_q;
  wire [10:0] f_imm11U;
  wire [15:0] imm16;
  wire [19:0] ALU_Result_q, increase_PC, multiplexer_1_out, NextPC_2_q, NextPC_q, PC, Target_Address;
  wire [31:0] AfterWrtieBus, aluResult, BeforeWrtieBus, bit_extender_1_out, BusA, BusB, Data_q, imm11_5S,
       imm16S, imm16Z, multiplexer_2_out, multiplexer_3_out, multiplexer_4_out, multiplexer_7_out, PC_1,
       ram_1_data, rd_imm5L_S, rd_imm11_shifted, register_1_q, register_file_1_busa, register_file_1_busb,
       rom_1_data;
  wire [31:20] ALU_Result_q_2;

  Clock clock_1 (.out(CLK));
  Adder #(.width(20)) adder_1 (.a(PC), .b(20'h1), .out(increase_PC));  // open: cin, cout
  // Probe on increase_PC
  // Probe on PC
  Register #(.width(20)) u_PC (.D(multiplexer_1_out), .en(Disable), .Q(PC), .clk(CLK));  // open: clr
  Multiplexer #(.width(20)) multiplexer_1 (
    .in0(increase_PC), .in1(Target_Address), .out(multiplexer_1_out), .sel(PCsrc));  // open: en
  not not_1 (Disable, Stall);
  ROM #(.addrWidth(20), .dataWidth(32)) rom_1 (.addr(PC), .data(rom_1_data));  // open: sel
  Multiplexer #(.width(32)) multiplexer_2 (
    .in0(rom_1_data), .in1({32{1'b0}}), .out(multiplexer_2_out), .sel(PCsrc));  // open: en
  Register #(.width(20)) NextPC (.D(PC), .Q(NextPC_q), .clk(CLK));  // open: en, clr
  Register #(.width(32)) Instruction (
    .D(multiplexer_2_out), .en(Disable), .Q({f_imm11U, rs2, rs1, rd_imm5L, OpCode}), .clk(CLK));  // open: clr
  D_Flip_Flop d_ff_1 (.clk(CLK), .D(control_unit_1_beq), .Q(BEQ));  // open: Qn, preset, en, reset
  D_Flip_Flop d_ff_2 (.clk(CLK), .D(control_unit_1_jalr), .Q(J));  // open: Qn, preset, en, reset
  Register #(.width(16)) u_Imm16 (.D({f_imm11U, rs2}), .Q(imm16), .clk(CLK));  // open: en, clr
  Control_Unit control_unit_1 (
    .OpCode(OpCode), .ALU_Op(control_unit_1_alu_op), .Function(f_imm11U),
    .Controller(control_unit_1_controller), .JALR(control_unit_1_jalr), .BEQ(control_unit_1_beq),
    .BNE(control_unit_1_bne), .BLT(control_unit_1_blt), .BGE(control_unit_1_bge), .BLTU(control_unit_1_bltu),
    .BGEU(control_unit_1_bgeu));
  D_Flip_Flop d_ff_3 (.clk(CLK), .D(control_unit_1_blt), .Q(BLT));  // open: Qn, preset, en, reset
  D_Flip_Flop d_ff_4 (.clk(CLK), .D(control_unit_1_bne), .Q(BNE));  // open: Qn, preset, en, reset
  D_Flip_Flop d_ff_5 (.clk(CLK), .D(control_unit_1_bltu), .Q(BLTU));  // open: Qn, preset, en, reset
  D_Flip_Flop d_ff_6 (.clk(CLK), .D(control_unit_1_bge), .Q(BGE));  // open: Qn, preset, en, reset
  Register_File register_file_1 (
    .RW(Rd4), .RA(rs1), .BusW(AfterWrtieBus), .RB(rs2), .Register_Write(RegWrite3),
    .BusB(register_file_1_busb), .BusA(register_file_1_busa));
  D_Flip_Flop d_ff_7 (.clk(CLK), .D(control_unit_1_bgeu), .Q(BGEU));  // open: Qn, preset, en, reset
  Multiplexer #(.select(2), .width(32)) multiplexer_3 (
    .in0(register_file_1_busa), .in1(aluResult), .in2(BeforeWrtieBus), .in3(AfterWrtieBus),
    .out(multiplexer_3_out), .sel(ForwardA));  // open: en
  Multiplexer #(.select(2), .width(32)) multiplexer_4 (
    .in0(register_file_1_busb), .in1(aluResult), .in2(BeforeWrtieBus), .in3(AfterWrtieBus),
    .out(multiplexer_4_out), .sel(ForwardB));  // open: en
  Multiplexer #(.width(7)) multiplexer_5 (
    .in0(control_unit_1_controller), .in1({7{1'b0}}), .out(multiplexer_5_out), .sel(or_1_out));  // open: en
  Multiplexer #(.width(7)) multiplexer_6 (
    .in0(control_unit_1_alu_op), .in1({7{1'b0}}), .out(multiplexer_6_out), .sel(or_1_out));  // open: en
  or or_1 (or_1_out, Kill2, Stall);
  Hazard_Detector hazard_detector_1 (
    .rs1(rs1), .rs2(rs2), .Rd2(Rd2), .Rd3(Rd3), .Rd4(Rd4), .RegWr1(RegWrite1), .RegWr2(RegWrite2),
    .RegWr3(RegWrite3), .ForwardA(ForwardA), .ForwardB(ForwardB), .EX_MemRd(EX_MemRd), .Stall(Stall));
  Register #(.width(20)) NextPC_2 (.D(NextPC_q), .Q(NextPC_2_q), .clk(CLK));  // open: en, clr
  Register #(.width(32)) A (.D(multiplexer_3_out), .Q(BusA), .clk(CLK));  // open: en, clr
  Register #(.width(32)) B (.D(multiplexer_4_out), .Q(BusB), .clk(CLK));  // open: en, clr
  Register #(.width(5)) u_Rd2 (.D(rd_imm5L), .Q(Rd2), .clk(CLK));  // open: en, clr
  Register #(.width(7)) EX (
    .D(multiplexer_5_out), .Q({RegWrite1, busBsrc, EX_q[3], EX_MemRd, EX_q[1:0]}), .clk(CLK));  // open: en, clr
  Register #(.width(7)) EX_2 (.D(multiplexer_6_out), .Q({EX_2_q, aluOP}), .clk(CLK));  // open: en, clr
  Multiplexer #(.select(2), .width(32)) multiplexer_7 (
    .in0(BusB), .in1(imm16S), .in2(imm16Z), .in3(register_1_q), .out(multiplexer_7_out), .sel(busBsrc));  // open: en
  Register #(.width(32)) register_1 (.D(imm11_5S), .Q(register_1_q), .clk(CLK));  // open: en, clr
  // Probe on Target_Address
  NextPC nextpc_3 (
    .Inc_PC(NextPC_2_q), .imm16(imm16), .Zero(Zero), .Target_Addres(Target_Address), .PCsrc_Kill1(PCsrc),
    .BNE(BNE), .J(J), .BQE(BEQ), .Ra(BusA), .BLT(BLT), .BGE(BGE), .BLTU(BLTU), .BGEU(BGEU),
    .Imm11_5S(imm11_5S), .Kill2(Kill2));
  ALU alu_1 (.A(BusA), .B(multiplexer_7_out), .ALU_Result(aluResult), .ALU_Selcetion(aluOP), .Zero(Zero));
  assign bit_extender_1_out = {{21{1'b0}}, f_imm11U};  // Bit_Extender bit_extender_1
  Register #(.width(32)) ALU_Result (.D(aluResult), .Q({ALU_Result_q_2, ALU_Result_q}), .clk(CLK));  // open: en, clr
  Register #(.width(32)) Data (.D(BusB), .Q(Data_q), .clk(CLK));  // open: en, clr
  Register #(.width(5)) u_Rd3 (.D(Rd2), .Q(Rd3), .clk(CLK));  // open: en, clr
  Register #(.width(7)) MEM (
    .D({RegWrite1, busBsrc, EX_q[3], EX_MemRd, EX_q[1:0]}), .Q({RegWrite2, MEM_q, MemW, MemR, busWsrc}),
    .clk(CLK));  // open: en, clr
  Shifter #(.width(32)) shifter_1 (.in(bit_extender_1_out), .\dist (5'b00101), .out(rd_imm11_shifted));
  assign rd_imm5L_S = {{27{rd_imm5L[4]}}, rd_imm5L};  // Bit_Extender bit_extender_2
  assign imm16S = {{16{imm16[15]}}, imm16};  // Bit_Extender bit_extender_3
  assign imm16Z = {{16{1'b0}}, imm16};  // Bit_Extender bit_extender_4
  // Probe on {ALU_Result_q_2, ALU_Result_q}
  RAM #(.addrWidth(20), .dataWidth(32), .bus("separate")) ram_1 (
    .addr(ALU_Result_q), .din(Data_q), .data(ram_1_data), .str(MemW), .clk(CLK), .ld(MemR), .clr(in_1));  // open: sel
  assign PC_1 = {{12{1'b0}}, increase_PC};  // Bit_Extender bit_extender_5
  Multiplexer #(.select(2), .width(32)) multiplexer_8 (
    .in0({ALU_Result_q_2, ALU_Result_q}), .in1(ram_1_data), .in2(PC_1), .out(BeforeWrtieBus), .sel(busWsrc));  // open: in3, en
  Register #(.width(32)) WriteBus (.D(BeforeWrtieBus), .Q(AfterWrtieBus), .clk(CLK));  // open: en, clr
  Register #(.width(5)) u_Rd4 (.D(Rd3), .Q(Rd4), .clk(CLK));  // open: en, clr
  Register #(.width(7)) WB (
    .D({RegWrite2, MEM_q, MemW, MemR, busWsrc}), .Q({RegWrite3, WB_q}), .clk(CLK));  // open: en, clr
  assign imm11_5S = rd_imm11_shifted | rd_imm5L_S;  // OR_Gate or_2, 32 bits wide

  // Other names for the same wires on the sheet: rd_imm5L_RG[4:0] = Rd4

  // Notes on the sheet:
  //   contents of rom_1 (hex, n*v repeats v):
  //   207c5 70145 1f2940 384e 3985 13185 384e 308e 800000 11212 800000 ffe62e91 800000 139c5 ffe53d51
  //   800000 14000d 2380f 1300f 5000d 14000d
endmodule
